// Logisim project control_logic.circ as structural Verilog: 1 circuit, main circuit control_logic
module control_logic (
  input  [31:0] inst,
  input  BrEq,
  input  BrLt,
  output PCSel,
  output RegWEn,
  output [2:0] ImmSel,
  output BrUn,
  output ASel,
  output BSel,
  output [3:0] ALUSel,
  output MemRW,
  output [1:0] WBSel,
  output CSRSel,
  output CSRWen
);

  wire and1, and_2_out, bsel13, func3_0, func3_1, func3_2, func3_3, func3_4, func3_5, func3_6, func3_7,
       func7_0, func7_1, func7_20, mul10, mulh14, mulhu11, multiplexer_1_out, multiplexer_2_out, or2,
       or_1_out, or_2_out, or_3_out, or_7_out, simple_logic, sll6, slt7, sra5, srl4, sub12, typeI, typeI13,
       typeI67, typeR, typeSB, typeU, typeU17, typeUJ, xor3;

  Comparator #(.mode("unsigned"), .width(7)) comparator_1 (.a(inst[6:0]), .b(7'b0110011), .eq(typeR));  // open: gt, lt
  Comparator #(.mode("unsigned"), .width(7)) comparator_2 (
    .a(inst[6:0]), .b(7'b0000011), .eq(WBSel[1]));  // open: gt, lt
  Comparator #(.mode("unsigned"), .width(7)) comparator_3 (
    .a(inst[6:0]), .b(7'b0010011), .eq(typeI13));  // open: gt, lt
  Comparator #(.mode("unsigned"), .width(7)) comparator_4 (
    .a(inst[6:0]), .b(7'b1100111), .eq(typeI67));  // open: gt, lt
  Comparator #(.mode("unsigned"), .width(7)) comparator_5 (.a(inst[6:0]), .b(7'b1110011), .eq(CSRWen));  // open: gt, lt
  Comparator #(.mode("unsigned"), .width(7)) comparator_6 (.a(inst[6:0]), .b(7'b0100011), .eq(MemRW));  // open: gt, lt
  Comparator #(.mode("unsigned"), .width(7)) comparator_7 (.a(inst[6:0]), .b(7'b1100011), .eq(typeSB));  // open: gt, lt
  Comparator #(.mode("unsigned"), .width(7)) comparator_8 (
    .a(inst[6:0]), .b(7'b0010111), .eq(typeU17));  // open: gt, lt
  Comparator #(.mode("unsigned"), .width(7)) comparator_9 (.a(inst[6:0]), .b(7'b0110111), .eq(bsel13));  // open: gt, lt
  Comparator #(.mode("unsigned"), .width(7)) comparator_10 (
    .a(inst[6:0]), .b(7'b1101111), .eq(typeUJ));  // open: gt, lt
  Comparator #(.mode("unsigned"), .width(3)) comparator_11 (.a(inst[14:12]), .b(3'b000), .eq(func3_0));  // open: gt, lt
  Comparator #(.mode("unsigned"), .width(3)) comparator_12 (.a(inst[14:12]), .b(3'b001), .eq(func3_1));  // open: gt, lt
  Comparator #(.mode("unsigned"), .width(3)) comparator_13 (.a(inst[14:12]), .b(3'b010), .eq(func3_2));  // open: gt, lt
  Comparator #(.mode("unsigned"), .width(3)) comparator_14 (.a(inst[14:12]), .b(3'b011), .eq(func3_3));  // open: gt, lt
  Comparator #(.mode("unsigned"), .width(3)) comparator_15 (.a(inst[14:12]), .b(3'b100), .eq(func3_4));  // open: gt, lt
  Comparator #(.mode("unsigned"), .width(3)) comparator_16 (.a(inst[14:12]), .b(3'b101), .eq(func3_5));  // open: gt, lt
  Comparator #(.mode("unsigned"), .width(3)) comparator_17 (.a(inst[14:12]), .b(3'b110), .eq(func3_6));  // open: gt, lt
  Comparator #(.mode("unsigned"), .width(3)) comparator_18 (.a(inst[14:12]), .b(3'b111), .eq(func3_7));  // open: gt, lt
  Comparator #(.mode("unsigned"), .width(7)) comparator_19 (
    .a(inst[31:25]), .b({7{1'b0}}), .eq(func7_0));  // open: gt, lt
  Comparator #(.mode("unsigned"), .width(7)) comparator_20 (
    .a(inst[31:25]), .b(7'b0000001), .eq(func7_1));  // open: gt, lt
  Comparator #(.mode("unsigned"), .width(7)) comparator_21 (
    .a(inst[31:25]), .b(7'b0100000), .eq(func7_20));  // open: gt, lt
  or or_1 (or_1_out, func3_6, func3_7);
  Multiplexer #(.enable("false")) multiplexer_1 (.in0(func3_1), .in1(func3_0), .out(multiplexer_1_out), .sel(BrEq));
  or or_2 (or_2_out, func3_5, func3_7);
  or or_3 (or_3_out, func3_4, func3_6);
  and and_1 (BrUn, typeSB, or_1_out);
  Multiplexer #(.enable("false")) multiplexer_2 (.in0(or_2_out), .in1(or_3_out), .out(multiplexer_2_out), .sel(BrLt));
  or or_4 (typeI, WBSel[1], typeI13, typeI67, CSRWen);
  or or_5 (typeU, typeU17, bsel13);
  nor nor_1 (ASel, typeR, WBSel[1], typeI13, MemRW, typeI67);
  not not_1 (BSel, typeR);
  or or_6 (PCSel, typeUJ, typeI67, and_2_out);
  or or_7 (or_7_out, multiplexer_1_out, multiplexer_2_out);
  nor nor_2 (RegWEn, MemRW, CSRWen, typeSB);
  nor nor_3 (WBSel[0], typeUJ, typeI67, WBSel[1]);
  Priority_Encoder priority_encoder_1 (
    .in0(typeI), .in1(MemRW), .in2(typeSB), .in3(typeU), .in4(typeUJ), .in7(typeR), .out(ImmSel));  // open: in5, in6, en_in, gs, en_out
  and and_2 (and_2_out, typeSB, or_7_out);
  or or_8 (simple_logic, typeR, typeI13);
  and and_3 (and1, func3_7, simple_logic);
  and and_4 (or2, func3_6, simple_logic);
  and and_5 (xor3, func3_4, simple_logic);
  and and_6 (srl4, func3_5, func7_0, simple_logic);
  and and_7 (sra5, func3_5, func7_20, simple_logic);
  and and_8 (sll6, func3_1, func7_0, simple_logic);
  and and_9 (slt7, func3_2, simple_logic);
  and and_10 (mul10, typeR, func3_0, func7_1);
  and and_11 (mulhu11, typeR, func3_3, func7_1);
  and and_12 (sub12, typeR, func3_0, func7_20);
  and and_13 (mulh14, typeR, func3_1, func7_1);
  and and_14 (CSRSel, CSRWen, func3_5);
  Priority_Encoder #(.select(4)) priority_encoder_2 (
    .in0(1'b1), .in1(and1), .in2(or2), .in3(xor3), .in4(srl4), .in5(sra5), .in6(sll6), .in7(slt7),
    .in10(mul10), .in11(mulhu11), .in12(sub12), .in13(bsel13), .in14(mulh14), .out(ALUSel));  // open: in8, in9, in15, gs, en_out, en_in

  // Other names for the same wires on the sheet: opcode[6:0] = inst[6:0]; func3[2:0] = inst[14:12];
  //   func7[6:0] = inst[31:25]; typeI_CSR = CSRWen; typeS = MemRW; typeU37 = bsel13; WBSel_bit0 = WBSel[0];
  //   typeI03 = WBSel[1]; WBSel_bit1 = WBSel[1]

  // Notes on the sheet:
  //   INPUTS to your circuit
  //   DON'T CHANGE THE LOCATIONS OF THE INPUTS AND OUTPUTS!
  //   OUTPUT from your circuit
endmodule
