// Logisim project cpu.circ as structural Verilog: 1 circuit, main circuit cpu
module cpu (
  input  clk,
  input  [31:0] INSTRUCTION,
  input  [31:0] READ_DATA,
  output [31:0] WRITE_ADDRESS,
  output [31:0] PROGRAM_COUNTER,
  output [31:0] ra,
  output [31:0] sp,
  output [31:0] t0,
  output [31:0] t1,
  output [31:0] t2,
  output [31:0] s0,
  output [31:0] s1,
  output [31:0] a0,
  output [31:0] tohost,
  output [3:0] WRITE_ENABLE,
  output [31:0] WRITE_DATA
);

  wire ASel, BrEq, BrLt, BrUn, BSel, control_logic_1_csrwen, control_logic_1_regwen, CSRSel, load_type,
       MemRW, PCSel;
  wire [1:0] WBSel;
  wire [2:0] control_logic_1_immsel, func3_cpu;
  wire [3:0] ALUSel, bit_extender_2_out, multiplexer_11_out, sb, sh;
  wire [4:0] dest;
  wire [6:0] inst;
  wire [7:0] multiplexer_9_out;
  wire [11:0] CSR_address;
  wire [15:0] multiplexer_10_out;
  wire [31:0] adder_2_out, bit_extender_5_out, CSR_data, CSR_imm, imm_gen_1_imm, lb, lh, load_data,
       multiplexer_1_out, multiplexer_2_out, multiplexer_3_out, multiplexer_4_out, multiplexer_12_out,
       PC_Plus_4, pipeline_PC, read_data_t, reg_write_data, rs1, rs2;

  Adder #(.width(32)) adder_1 (.a(PROGRAM_COUNTER), .b(32'h4), .out(PC_Plus_4));  // open: cin, cout
  Register #(.width(32)) PC (.D(multiplexer_1_out), .clk(clk), .Q(PROGRAM_COUNTER));  // open: en, clr
  Multiplexer #(.enable("false"), .width(32)) multiplexer_1 (
    .in0(PC_Plus_4), .in1(WRITE_ADDRESS), .out(multiplexer_1_out), .sel(PCSel));
  Register #(.width(32)) register_1 (
    .D(multiplexer_2_out), .clk(clk), .Q({CSR_address, CSR_imm[4:0], func3_cpu, dest, inst}));  // open: en, clr
  Multiplexer #(.enable("false"), .width(32)) multiplexer_2 (
    .in0(INSTRUCTION), .in1(32'h13), .out(multiplexer_2_out), .sel(PCSel));
  Register #(.width(32)) register_2 (.D(PROGRAM_COUNTER), .clk(clk), .Q(pipeline_PC));  // open: en, clr
  control_logic control_logic_1 (
    .CSRWen(control_logic_1_csrwen), .PCSel(PCSel), .RegWEn(control_logic_1_regwen),
    .ImmSel(control_logic_1_immsel), .BrUn(BrUn), .ASel(ASel), .BSel(BSel), .ALUSel(ALUSel), .MemRW(MemRW),
    .WBSel(WBSel), .CSRSel(CSRSel), .inst({CSR_address, CSR_imm[4:0], func3_cpu, dest, inst}), .BrEq(BrEq),
    .BrLt(BrLt));
  regfile regfile_1 (
    .rs1(CSR_imm[4:0]), .rs2(CSR_address[4:0]), .rd(dest), .Write_Data(reg_write_data),
    .RegWEn(control_logic_1_regwen), .clk(clk), .ra(ra), .sp(sp), .t0(t0), .t1(t1), .t2(t2), .s0(s0),
    .s1(s1), .a0(a0), .Read_Data_1(rs1), .Read_Data_2(rs2));
  imm_gen imm_gen_1 (
    .inst({CSR_address, CSR_imm[4:0], func3_cpu, dest, inst}), .ImmSel(control_logic_1_immsel),
    .imm(imm_gen_1_imm));
  branch_comp branch_comp_1 (.rs1(rs1), .rs2(rs2), .BrUn(BrUn), .BrEq(BrEq), .BrLt(BrLt));
  assign CSR_imm[31:5] = {{26{1'b0}}, 1'b0};  // Bit_Extender bit_extender_1
  Multiplexer #(.enable("false"), .width(32)) multiplexer_3 (
    .in0(rs1), .in1(pipeline_PC), .out(multiplexer_3_out), .sel(ASel));
  Multiplexer #(.enable("false"), .width(32)) multiplexer_4 (
    .in0(rs2), .in1(imm_gen_1_imm), .out(multiplexer_4_out), .sel(BSel));
  alu alu_1 (.Result(WRITE_ADDRESS), .A(multiplexer_3_out), .B(multiplexer_4_out), .ALUSel(ALUSel));
  csr csr_1 (
    .CSR_address(CSR_address), .CSR_din(CSR_data), .CSR_WE(control_logic_1_csrwen), .clk(clk), .tohost(tohost));
  Multiplexer #(.enable("false"), .width(32)) multiplexer_5 (.in0(rs1), .in1(CSR_imm), .out(CSR_data), .sel(CSRSel));
  Shifter #(.width(32)) shifter_1 (.in(rs2), .\dist ({WRITE_ADDRESS[1:0], 3'b000}), .out(WRITE_DATA));
  Adder #(.width(32)) adder_2 (.a(pipeline_PC), .b(32'h4), .out(adder_2_out));  // open: cin, cout
  Multiplexer #(.enable("false"), .select(2), .width(32)) multiplexer_6 (
    .in0(adder_2_out), .in1(WRITE_ADDRESS), .in2(read_data_t), .out(reg_write_data), .sel(WBSel));  // open: in3
  Multiplexer #(.enable("false"), .select(2), .width(4)) multiplexer_7 (
    .in0(4'b0001), .in1(4'b0010), .in2(4'b0100), .in3(4'b1000), .out(sb), .sel(WRITE_ADDRESS[1:0]));
  Multiplexer #(.enable("false"), .select(2), .width(4)) multiplexer_8 (
    .in0(4'b0011), .in1(4'b0110), .in2(4'b1100), .out(sh), .sel(WRITE_ADDRESS[1:0]));  // open: in3
  Multiplexer #(.enable("false"), .select(2), .width(8)) multiplexer_9 (
    .in0(READ_DATA[7:0]), .in1(READ_DATA[15:8]), .in2(READ_DATA[23:16]), .in3(READ_DATA[31:24]),
    .out(multiplexer_9_out), .sel(WRITE_ADDRESS[1:0]));
  Multiplexer #(.enable("false"), .select(2), .width(16)) multiplexer_10 (
    .in0(READ_DATA[15:0]), .in1(READ_DATA[23:8]), .in2(READ_DATA[31:16]), .out(multiplexer_10_out),
    .sel(WRITE_ADDRESS[1:0]));  // open: in3
  assign bit_extender_2_out = {{3{MemRW}}, MemRW};  // Bit_Extender bit_extender_2
  Multiplexer #(.enable("false"), .select(2), .width(4)) multiplexer_11 (
    .in0(sb), .in1(sh), .in2(4'b1111), .out(multiplexer_11_out), .sel(func3_cpu[1:0]));  // open: in3
  assign lb = {{24{multiplexer_9_out[7]}}, multiplexer_9_out};  // Bit_Extender bit_extender_3
  assign lh = {{16{multiplexer_10_out[15]}}, multiplexer_10_out};  // Bit_Extender bit_extender_4
  assign WRITE_ENABLE = bit_extender_2_out & multiplexer_11_out;  // AND_Gate and_1, 4 bits wide
  Comparator #(.mode("unsigned"), .width(7)) comparator_1 (.a(inst), .b(7'b0000011), .eq(load_type));  // open: gt, lt
  assign bit_extender_5_out = {{31{load_type}}, load_type};  // Bit_Extender bit_extender_5
  Multiplexer #(.enable("false"), .select(2), .width(32)) multiplexer_12 (
    .in0(lb), .in1(lh), .in2(READ_DATA), .out(multiplexer_12_out), .sel(func3_cpu[1:0]));  // open: in3
  Multiplexer #(.enable("false"), .width(32)) multiplexer_13 (
    .in0(READ_DATA), .in1(load_data), .out(read_data_t), .sel(load_type));
  assign load_data = bit_extender_5_out & multiplexer_12_out;  // AND_Gate and_2, 32 bits wide

  // Other names for the same wires on the sheet: ALU_offset[1:0] = WRITE_ADDRESS[1:0];
  //   ALU_Output[31:0] = WRITE_ADDRESS; inst[31:7] = {CSR_address, CSR_imm[4:0], func3_cpu, dest};
  //   read_reg1[4:0] = CSR_imm[4:0]; opcode_cpu[6:0] = inst; read_reg2[4:0] = CSR_address[4:0]

  // Notes on the sheet:
  //   Output to IMEM
  //   IMEM (do **NOT** move this)
  //   Inputs from IMEM
  //   It is OK to move the PC, RegFile, ALU, MEM, Branch Comp, Imm Gen, and Control Logic to wherever is most convenient for you when constructing your CPU, and to delete this text
  //   Inputs/Outputs for testing. Do **NOT** move these.
  //   Outputs To DMEM
  //   DMEM (do **NOT** move this)
  //   Inputs From DMEM
  //   Store Byte
  //   Store Half-Word
  //   Store Word
  //   Load Byte
  //   Load Half-Word
endmodule
