// Logisim project imm_gen.circ as structural Verilog: 1 circuit, main circuit imm_gen
module imm_gen (
  input  [31:0] inst,
  input  [2:0] ImmSel,
  output [31:0] imm
);

  wire [11:0] bit_extender_4_out, bit_extender_5_out;
  wire [19:0] bit_extender_3_out;
  wire [20:0] bit_extender_1_out, bit_extender_2_out;

  assign bit_extender_1_out = {{20{inst[31]}}, inst[31]};  // Bit_Extender bit_extender_1
  assign bit_extender_2_out = {{20{inst[31]}}, inst[31]};  // Bit_Extender bit_extender_2
  assign bit_extender_3_out = {{19{inst[31]}}, inst[31]};  // Bit_Extender bit_extender_3
  assign bit_extender_4_out = {{11{1'b0}}, 1'b0};  // Bit_Extender bit_extender_4
  assign bit_extender_5_out = {{11{inst[31]}}, inst[31]};  // Bit_Extender bit_extender_5
  Multiplexer #(.enable("false"), .select(3), .width(32)) multiplexer_1 (
    .in0({bit_extender_1_out, inst[30:20]}), .in1({bit_extender_2_out, inst[30:25], inst[11:7]}),
    .in2({bit_extender_3_out, inst[7], inst[30:25], inst[11:8], 1'b0}),
    .in3({inst[31:12], bit_extender_4_out}),
    .in4({bit_extender_5_out, inst[19:12], inst[20], inst[30:21], 1'b0}), .out(imm), .sel(ImmSel));  // open: in5, in6, in7

  // Notes on the sheet:
  //   INPUTS to your circuit
  //   DON'T CHANGE THE LOCATIONS OF THE INPUTS AND OUTPUTS!
  //   OUTPUT from your circuit
endmodule
