// Logisim project regfile.circ as structural Verilog: 1 circuit, main circuit regfile
module regfile (
  input  [4:0] rs1,
  input  [4:0] rs2,
  input  [4:0] rd,
  input  [31:0] Write_Data,
  input  RegWEn,
  input  clk,
  output [31:0] ra,
  output [31:0] sp,
  output [31:0] t0,
  output [31:0] t1,
  output [31:0] t2,
  output [31:0] s0,
  output [31:0] s1,
  output [31:0] a0,
  output [31:0] Read_Data_1,
  output [31:0] Read_Data_2
);

  wire x1_in, x2_in, x3_in, x4_in, x5_in, x6_in, x7_in, x8_in, x9_in, x10_in, x11_in, x12_in, x13_in, x14_in,
       x15_in, x16_in, x17_in, x18_in, x19_in, x20_in, x21_in, x22_in, x23_in, x24_in, x25_in, x26_in,
       x27_in, x28_in, x29_in, x30_in, x31_in;
  wire [31:0] x3_out, x4_out, x11_out, x12_out, x13_out, x14_out, x15_out, x16_out, x17_out, x18_out,
       x19_out, x20_out, x21_out, x22_out, x23_out, x24_out, x25_out, x26_out, x27_out, x28_out, x29_out,
       x30_out, x31_out;

  Demultiplexer #(.enable("false"), .select(5)) demultiplexer_1 (
    .out1(x1_in), .out2(x2_in), .out3(x3_in), .out4(x4_in), .out5(x5_in), .out6(x6_in), .out7(x7_in),
    .out8(x8_in), .out9(x9_in), .out10(x10_in), .out11(x11_in), .out12(x12_in), .out13(x13_in),
    .out14(x14_in), .out15(x15_in), .out16(x16_in), .out17(x17_in), .out18(x18_in), .out19(x19_in),
    .out20(x20_in), .out21(x21_in), .out22(x22_in), .out23(x23_in), .out24(x24_in), .out25(x25_in),
    .out26(x26_in), .out27(x27_in), .out28(x28_in), .out29(x29_in), .out30(x30_in), .out31(x31_in),
    .in(RegWEn), .sel(rd));  // open: out0
  Register #(.width(32)) register_1 (.D(Write_Data), .en(x1_in), .clk(clk), .Q(ra));  // open: clr
  Register #(.width(32)) register_2 (.D(Write_Data), .en(x2_in), .clk(clk), .Q(sp));  // open: clr
  Register #(.width(32)) register_3 (.D(Write_Data), .en(x3_in), .clk(clk), .Q(x3_out));  // open: clr
  Register #(.width(32)) register_4 (.D(Write_Data), .en(x4_in), .clk(clk), .Q(x4_out));  // open: clr
  Register #(.width(32)) register_5 (.D(Write_Data), .en(x5_in), .clk(clk), .Q(t0));  // open: clr
  Register #(.width(32)) register_6 (.D(Write_Data), .en(x6_in), .clk(clk), .Q(t1));  // open: clr
  Register #(.width(32)) register_7 (.D(Write_Data), .en(x7_in), .clk(clk), .Q(t2));  // open: clr
  Register #(.width(32)) register_8 (.D(Write_Data), .en(x8_in), .clk(clk), .Q(s0));  // open: clr
  Register #(.width(32)) register_9 (.D(Write_Data), .en(x9_in), .clk(clk), .Q(s1));  // open: clr
  Register #(.width(32)) register_10 (.D(Write_Data), .en(x10_in), .clk(clk), .Q(a0));  // open: clr
  Register #(.width(32)) register_11 (.D(Write_Data), .en(x11_in), .clk(clk), .Q(x11_out));  // open: clr
  Register #(.width(32)) register_12 (.D(Write_Data), .en(x12_in), .clk(clk), .Q(x12_out));  // open: clr
  Register #(.width(32)) register_13 (.D(Write_Data), .en(x13_in), .clk(clk), .Q(x13_out));  // open: clr
  Register #(.width(32)) register_14 (.D(Write_Data), .en(x14_in), .clk(clk), .Q(x14_out));  // open: clr
  Register #(.width(32)) register_15 (.D(Write_Data), .en(x15_in), .clk(clk), .Q(x15_out));  // open: clr
  Register #(.width(32)) register_16 (.D(Write_Data), .en(x16_in), .clk(clk), .Q(x16_out));  // open: clr
  Register #(.width(32)) register_17 (.D(Write_Data), .en(x17_in), .clk(clk), .Q(x17_out));  // open: clr
  Register #(.width(32)) register_18 (.D(Write_Data), .en(x18_in), .clk(clk), .Q(x18_out));  // open: clr
  Register #(.width(32)) register_19 (.D(Write_Data), .en(x19_in), .clk(clk), .Q(x19_out));  // open: clr
  Register #(.width(32)) register_20 (.D(Write_Data), .en(x20_in), .clk(clk), .Q(x20_out));  // open: clr
  Register #(.width(32)) register_21 (.D(Write_Data), .en(x21_in), .clk(clk), .Q(x21_out));  // open: clr
  Register #(.width(32)) register_22 (.D(Write_Data), .en(x22_in), .clk(clk), .Q(x22_out));  // open: clr
  Register #(.width(32)) register_23 (.D(Write_Data), .en(x23_in), .clk(clk), .Q(x23_out));  // open: clr
  Register #(.width(32)) register_24 (.D(Write_Data), .en(x24_in), .clk(clk), .Q(x24_out));  // open: clr
  Register #(.width(32)) register_25 (.D(Write_Data), .en(x25_in), .clk(clk), .Q(x25_out));  // open: clr
  Register #(.width(32)) register_26 (.D(Write_Data), .en(x26_in), .clk(clk), .Q(x26_out));  // open: clr
  Register #(.width(32)) register_27 (.D(Write_Data), .en(x27_in), .clk(clk), .Q(x27_out));  // open: clr
  Register #(.width(32)) register_28 (.D(Write_Data), .en(x28_in), .clk(clk), .Q(x28_out));  // open: clr
  Register #(.width(32)) register_29 (.D(Write_Data), .en(x29_in), .clk(clk), .Q(x29_out));  // open: clr
  Register #(.width(32)) register_30 (.D(Write_Data), .en(x30_in), .clk(clk), .Q(x30_out));  // open: clr
  Register #(.width(32)) register_31 (.D(Write_Data), .en(x31_in), .clk(clk), .Q(x31_out));  // open: clr
  Multiplexer #(.enable("false"), .select(5), .width(32)) multiplexer_1 (
    .in0({32{1'b0}}), .in1(ra), .in2(sp), .in3(x3_out), .in4(x4_out), .in5(t0), .in6(t1), .in7(t2), .in8(s0),
    .in9(s1), .in10(a0), .in11(x11_out), .in12(x12_out), .in13(x13_out), .in14(x14_out), .in15(x15_out),
    .in16(x16_out), .in17(x17_out), .in18(x18_out), .in19(x19_out), .in20(x20_out), .in21(x21_out),
    .in22(x22_out), .in23(x23_out), .in24(x24_out), .in25(x25_out), .in26(x26_out), .in27(x27_out),
    .in28(x28_out), .in29(x29_out), .in30(x30_out), .in31(x31_out), .out(Read_Data_1), .sel(rs1));
  Multiplexer #(.enable("false"), .select(5), .width(32)) multiplexer_2 (
    .in0({32{1'b0}}), .in1(ra), .in2(sp), .in3(x3_out), .in4(x4_out), .in5(t0), .in6(t1), .in7(t2), .in8(s0),
    .in9(s1), .in10(a0), .in11(x11_out), .in12(x12_out), .in13(x13_out), .in14(x14_out), .in15(x15_out),
    .in16(x16_out), .in17(x17_out), .in18(x18_out), .in19(x19_out), .in20(x20_out), .in21(x21_out),
    .in22(x22_out), .in23(x23_out), .in24(x24_out), .in25(x25_out), .in26(x26_out), .in27(x27_out),
    .in28(x28_out), .in29(x29_out), .in30(x30_out), .in31(x31_out), .out(Read_Data_2), .sel(rs2));

  // Other names for the same wires on the sheet: read_data1[31:0] = Read_Data_1; read_data2[31:0] = Read_Data_2;
  //   read_reg1[4:0] = rs1; read_reg2[4:0] = rs2; write_en = RegWEn; write_reg[4:0] = rd; x1_out[31:0] = ra;
  //   x2_out[31:0] = sp; x5_out[31:0] = t0; x6_out[31:0] = t1; x7_out[31:0] = t2; x8_out[31:0] = s0;
  //   x9_out[31:0] = s1; x10_out[31:0] = a0

  // Notes on the sheet:
  //   INPUTS to your circuit
  //   DON'T CHANGE THE LOCATIONS OF THE INPUTS AND OUTPUTS!
  //   These are DEBUG/TEST outputs from your circuit.
  //   OUTPUTS from your circuit
endmodule
