// Logisim project cpu-cpu-simple_SB_type.circ as structural Verilog: 1 circuit, main circuit run_main
module run_main (
  output [31:0] ra,
  output [31:0] sp,
  output [31:0] t0,
  output [31:0] t1,
  output [31:0] t2,
  output [31:0] s0,
  output [31:0] s1,
  output [31:0] a0,
  output [31:0] Requested_Address,
  output [31:0] Requested_Instruction,
  output [15:0] Time_Step,
  output halt
);

  wire clk;

  Clock clock_1 (.out(clk));
  // Probe on Requested_Address
  // test_harness test_harness_1: pin names not known; wires that end beside it: Requested_Instruction, clk, Requested_Address, ra, sp, t0, t1, t2, s0, s1, a0
  ROM #(.addrWidth(14), .dataWidth(32)) rom_1 (.addr(Requested_Address[15:2]), .data(Requested_Instruction));
  // Probe on Requested_Instruction
  Counter #(.max('hffff), .width(16)) counter_1 (.clk(clk), .Q(Time_Step));  // open: clr, load, up, count, D, carry
  Comparator #(.width(16)) comparator_1 (.a(Time_Step), .b(16'h31), .eq(halt));  // open: gt, lt

  // Other names for the same wires on the sheet: fetch_addr[31:0] = Requested_Address;
  //   Instruction[31:0] = Requested_Instruction

  // Notes on the sheet:
  //   contents of rom_1 (hex, n*v repeats v):
  //   00000493 00000913 01248463 00400313 012482B3 FFD00313 00200393 FE7308E3 02730E33 FF600E93 FF400F13
  //   FFEE80E3 01EE9263 00730FB3 FE949EE3 08500F93 08500F13 FDFF16E3 01EEC263 00C00993 FE9F4EE3 FFEFCCE3
  //   009F5263 00900993 00900A13 F9C00A93 F9C00B13 FF3AD0E3 FD49EEE3 01EA6263 00000993 FF6AEEE3 0149F263
  //   03348BB3 00499C13 FFEA76E3 01EFF263 00900C93 F8800B93 017B7263 00000493
  //   Instruction Memory
  //   Halts Execution After Constant # of Clock Cycles
  //   Constant
endmodule
