// Logisim project cpu-simple_all_registers.circ as structural Verilog: 1 circuit, main circuit run_main
module run_main (
  output [31:0] ra,
  output [31:0] sp,
  output [31:0] t0,
  output [31:0] t1,
  output [31:0] t2,
  output [31:0] s0,
  output [31:0] s1,
  output [31:0] a0,
  output [31:0] Requested_Address,
  output [31:0] Requested_Instruction,
  output [15:0] Time_Step,
  output halt
);

  wire clk;

  Clock clock_1 (.out(clk));
  // Probe on Requested_Address
  // test_harness test_harness_1: pin names not known; wires that end beside it: Requested_Instruction, clk, Requested_Address, ra, sp, t0, t1, t2, s0, s1, a0
  ROM #(.addrWidth(14), .dataWidth(32)) rom_1 (.addr(Requested_Address[15:2]), .data(Requested_Instruction));
  // Probe on Requested_Instruction
  Counter #(.max('hffff), .width(16)) counter_1 (.clk(clk), .Q(Time_Step));  // open: clr, load, up, count, D, carry
  Comparator #(.width(16)) comparator_1 (.a(Time_Step), .b(16'h3f), .eq(halt));  // open: gt, lt

  // Other names for the same wires on the sheet: fetch_addr[31:0] = Requested_Address;
  //   Instruction[31:0] = Requested_Instruction

  // Notes on the sheet:
  //   contents of rom_1 (hex, n*v repeats v):
  //   00000013 FFF00093 FFE00113 FFD00193 FFC00213 FFB00293 FFA00313 FF900393 00800413 00800493 00A00513
  //   00B00593 00C00613 00D00693 00E00713 00F00793 01000813 01100893 01200913 01300993 01400A13 01500A93
  //   01600B13 01700B93 01800C13 01900C93 01A00D13 01B00D93 01C00E13 01D00E93 01E00F13 01F00F93 00E692B3
  //   00D712B3 003F92B3 01D312B3 004312B3 009412B3 00D72333 00E6A333 003FA333 01D32333 00432333 00942333
  //   00D753B3 00E6D3B3 003FD3B3 01D353B3 004353B3 009453B3 40D75533 40E6D533 403FD533 41D35533 40435533
  //   40945533 00469293 00772313 FF96A313 00975393 40A75513
  //   Instruction Memory
  //   Halts Execution After Constant # of Clock Cycles
  //   Constant
endmodule
