// Logisim project cpu-simple_sb.circ as structural Verilog: 1 circuit, main circuit run_main
module run_main (
  output [31:0] ra,
  output [31:0] sp,
  output [31:0] t0,
  output [31:0] t1,
  output [31:0] t2,
  output [31:0] s0,
  output [31:0] s1,
  output [31:0] a0,
  output [31:0] Requested_Address,
  output [31:0] Requested_Instruction,
  output [15:0] Time_Step,
  output halt
);

  wire clk;

  Clock clock_1 (.out(clk));
  // Probe on Requested_Address
  // test_harness test_harness_1: pin names not known; wires that end beside it: Requested_Instruction, clk, Requested_Address, ra, sp, t0, t1, t2, s0, s1, a0
  ROM #(.addrWidth(14), .dataWidth(32)) rom_1 (.addr(Requested_Address[15:2]), .data(Requested_Instruction));
  // Probe on Requested_Instruction
  Counter #(.max('hffff), .width(16)) counter_1 (.clk(clk), .Q(Time_Step));  // open: clr, load, up, count, D, carry
  Comparator #(.width(16)) comparator_1 (.a(Time_Step), .b(16'h17), .eq(halt));  // open: gt, lt

  // Other names for the same wires on the sheet: fetch_addr[31:0] = Requested_Address;
  //   Instruction[31:0] = Requested_Instruction

  // Notes on the sheet:
  //   contents of rom_1 (hex, n*v repeats v):
  //   3E810113 1C800F13 E7E10823 E7010283 EDE10A23 ED410303 F3E10C23 F3810383 F9E10E23 F9C10503 01E10023
  //   00010483 07E10223 06410383 0DE10423 0C810E03 13E10623 12C10E83 03C383B3 03D383B3 02730333
  //   Instruction Memory
  //   Halts Execution After Constant # of Clock Cycles
  //   Constant
endmodule
